# Fritzing sketch eindopdracht (saved by Fritzing 0.9.3b)
breadboards: 3

parts:
  Part1 = Arduino Nano (Rev3.0) (ICSP)
  IC1 = SHIFT REGISTER [package=dil16]
  IC2 = SHIFT REGISTER [package=dil16]
  Disp1 = LBT2088AH [part_number=LBT2088AH]
  DS1 = DS18B20 1-Wire Temperature Sensor [part_number=DS18B20]
  R1 = Resistor [tolerance=±5% resistance=220 package="0603 [SMD]"]

nets:
  GND: Part1.GND, IC1.GND, IC1.G, IC2.GND, IC2.G, DS1.GND
  N1: Part1.D4, IC2.SER
  N2: Part1.D5, IC2.SCK
  N3: Part1.D6, IC2.RCK
  N4: Part1.D8, IC1.SER
  N5: Part1.D9, IC1.SCK
  N6: Part1.D10, IC1.RCK
  VCC: Part1.5V, IC1.SCL, IC1.VCC, IC2.SCL, IC2.VCC, DS1.VDD, R1.Pin_0
  N7: Part1.A0, DS1.DQ, R1.Pin_1
  N8: IC1.QB, Disp1.pin2
  N9: IC1.QC, Disp1.pin_7
  N10: IC1.QD, Disp1.pin1
  N11: IC1.QE, Disp1.pin_12
  N12: IC1.QF, Disp1.pin_8
  N13: IC1.QG, Disp1.pin_14
  N14: IC1.QH, Disp1.pin_9
  N15: IC1.QA, Disp1.pin_5
  N16: IC2.QB, Disp1.pin_3
  N17: IC2.QC, Disp1.pin_4
  N18: IC2.QD, Disp1.pin_10
  N19: IC2.QE, Disp1.pin_6
  N20: IC2.QF, Disp1.pin_11
  N21: IC2.QG, Disp1.pin_15
  N22: IC2.QH, Disp1.pin_16
  N23: IC2.QA, Disp1.pin_13
