# Fritzing sketch opdr2 (saved by Fritzing 0.9.3b)
breadboards: 1

parts:
  Part1 = Arduino Nano (Rev3.0)
  DI1 = 7-Segment LED Display [package=THT]
  DI2 = 7-Segment LED Display [package=THT]
  R1 = Resistor [tolerance=±5% resistance=220 package="1206 [SMD]"]

nets:
  N1: Part1.D2, DI2.commAnode#2
  N2: Part1.D3, DI1.cathodeC
  N3: Part1.D4, DI2.cathodeC
  N4: Part1.D5, DI2.cathodeDP
  N5: Part1.D8, DI2.cathodeG
  N6: Part1.D9, DI2.commAnode#7
  N7: Part1.D10, DI2.cathodeA
  N8: Part1.D11/MOSI, DI2.cathodeF
  N9: Part1.D12/MISO, DI2.cathodeE
  N10: Part1.A5, DI1.commAnode#2
  N11: Part1.A4, DI1.cathodeD
  N12: Part1.A3, DI1.cathodeE
  N13: Part1.A2, DI1.cathodeA
  N14: Part1.A1, DI1.commAnode#7
  N15: Part1.A0, DI1.cathodeF
  N16: Part1.3V3, DI1.cathodeG, DI2.cathodeB, R1.Pin_0, R1.Pin_1
  N17: Part1.D13/SCK, DI2.cathodeD
