# Fritzing sketch opdr3a (saved by Fritzing 0.9.3b)
breadboards: 1

parts:
  Part1 = Arduino Nano (Rev3.0) (ICSP)
  LED1 = LEDs [package=led10mm]
  LED2 = LEDs [package=led10mm]
  LED3 = LEDs [package=led10mm]
  LED4 = LEDs [package=led10mm]
  LED5 = LEDs [package=led10mm]
  LED6 = LEDs [package=led10mm]
  LED7 = LEDs [package=led10mm]
  LED8 = LEDs [package=led10mm]
  LED9 = LEDs [package=led10mm]
  R1 = Resistor [tolerance=±5% resistance=220 package="0402 [SMD]"]
  R2 = Resistor [tolerance=±5% resistance=220 package="0603 [SMD]"]
  R3 = Resistor [tolerance=±5% resistance=220 package="0603 [SMD]"]
  R4 = Resistor [tolerance=±5% resistance=220 package="0603 [SMD]"]
  R5 = Resistor [tolerance=±5% resistance=220 package="0603 [SMD]"]
  R6 = Resistor [tolerance=±5% resistance=220 package="0603 [SMD]"]
  R7 = Resistor [tolerance=±5% resistance=220 package="0603 [SMD]"]
  R9 = Resistor [tolerance=±5% resistance=220 package="0603 [SMD]"]
  R10 = Resistor [tolerance=±5% resistance=220 package="0402 [SMD]"]
  R11 = Resistor [tolerance=±5% resistance=220 package="0402 [SMD]"]
  S1 = Pushbutton [package=THT]

nets:
  N1: Part1.GND, Part1.A0, R1.Pin_0, R2.Pin_0, R3.Pin_0, R7.Pin_0, S1.leg0, S1.leg1
  N2: Part1.D4, LED3.A
  N3: Part1.D5, LED4.A
  N4: Part1.D6, LED1.A
  N5: Part1.D7, LED5.A
  N6: Part1.D8, LED2.A
  N7: Part1.D9, LED7.A
  N8: Part1.D10, LED8.A
  N9: Part1.D11/MOSI, LED9.A
  N10: Part1.D12/MISO, LED6.A
  N11: Part1.3V3, R11.Pin_1
  N12: LED1.C, R1.Pin_1
  N13: LED2.C, R2.Pin_1
  N14: LED3.C, R3.Pin_1
  N15: LED4.C, R9.Pin_1
  N16: LED5.C, R5.Pin_1
  N17: LED6.C, R4.Pin_1
  N18: LED7.C, R10.Pin_1
  N19: LED8.C, R7.Pin_1
  N20: LED9.C, R6.Pin_1
  N21: R4.Pin_0, R5.Pin_0, R6.Pin_0, R9.Pin_0, R10.Pin_0, R11.Pin_0
