# Fritzing sketch opdr3b (saved by Fritzing 0.9.3b)
breadboards: 1

parts:
  Part1 = Arduino Nano (Rev3.0) (ICSP)
  C1 = Capacitor Polarized [package=panasonic_g]
  SP1 = SPEAKER [package=pcb_mount_speaker]
  R1 = Resistor [tolerance=±5% resistance=220 package="0805 [SMD]"]
  R2 = Rotary Potentiometer (Large) [maximum_resistance=100kΩ package=THT]

nets:
  N1: Part1.GND, C1.+, C1.-, SP1.+, SP1.-, R1.Pin_0, R2.leg2
  N2: Part1.D6, R1.Pin_1
  N3: Part1.5V, R2.leg1
  N4: Part1.A0, R2.wiper
