# Fritzing sketch opdr4 (saved by Fritzing 0.9.3b)
breadboards: 1

parts:
  Part1 = Arduino Nano (Rev3.0) (ICSP)
  LED1 = RGB LED - (4 legs) [package="5 mm [THT]"]
  R1 = Resistor [tolerance=±5% resistance=220 package=THT]  # not connected
  R2 = Resistor [tolerance=±5% resistance=220 package=THT]
  R3 = Resistor [tolerance=±5% resistance=220 package=THT]

nets:
  N1: Part1.D10, R3.Pin_0
  N2: Part1.D11/MOSI, R2.Pin_0
  N3: Part1.5V, LED1.green_cathode
  N4: LED1.common_anode, R3.Pin_1
  N5: LED1.blue_cathode, R2.Pin_1
