# Fritzing sketch opdr4c (saved by Fritzing 0.9.3b)
breadboards: 1

parts:
  Part1 = Arduino Nano (Rev3.0)
  R1 = Resistor [tolerance=±5% resistance=220 package="0402 [SMD]"]
  R2 = Resistor [tolerance=±5% resistance=220 package="0402 [SMD]"]
  R3 = Resistor [tolerance=±5% resistance=220 package="0402 [SMD]"]
  R4 = Resistor [tolerance=±5% resistance=220 package="0402 [SMD]"]
  LED1 = RGB LED (com. cathode, rbg) [package="5 mm [THT]"]

nets:
  N1: Part1.D10, R1.Pin_1
  N2: Part1.D12/MISO, R2.Pin_0
  N3: Part1.3V3, R4.Pin_0, R4.Pin_1, LED1.common_cathode
  N4: R1.Pin_0, LED1.green_anode
  N5: R2.Pin_1, LED1.blue_anode
  N6: R3.Pin_1, LED1.red_anode
