# Fritzing sketch opdr5b (saved by Fritzing 0.9.3b)
breadboards: 1

parts:
  Part1 = Arduino Nano (Rev3.0)
  LCD1 = LCD screen
  U1 = POT_SWITCH [package=pot_pth]

nets:
  GND: Part1.GND, LCD1.VSS, LCD1.R/W, LCD1.LED-
  5V: Part1.5V, LCD1.VDD
  N1: Part1.A5, LCD1.E
  N2: Part1.A4, LCD1.RS
  N3: Part1.A3, LCD1.DB7
  N4: Part1.A2, LCD1.DB6
  N5: Part1.A1, LCD1.DB5
  N6: Part1.A0, LCD1.DB4
  N7: LCD1.V0, U1.G$2_1
  N8: LCD1.LED+, U1.G$1_A
